# Fritzing sketch ArduinoSID r7 (saved by Fritzing 0.9.3b)
circuit board: 5.86903cm x 5.02193cm
breadboards: 1

parts:
  Arduino_Nano = Arduino Nano (Rev3.0)
  Audio_Out = 3.5mm Audio Jack [package=audio-jack]
  C1 = Electrolytic Capacitor [capacitance=1µF package="100 mil [THT, electrolytic]"]
  SwinSid_Ultimate = IC, DIP package, 28 pins [chip_label="SwinSID Ultimate"]
  C2 = Electrolytic Capacitor [capacitance=1µF package="100 mil [THT, electrolytic]"]
  C3 = Electrolytic Capacitor [capacitance=1µF package="100 mil [THT, electrolytic]"]

nets:
  GND: Arduino_Nano.GND, Audio_Out.SLEEVE, SwinSid_Ultimate.pin14
  N1: Arduino_Nano.D2, SwinSid_Ultimate.pin17
  N2: Arduino_Nano.D3, SwinSid_Ultimate.pin18
  N3: Arduino_Nano.D4, SwinSid_Ultimate.pin19
  N4: Arduino_Nano.D5, SwinSid_Ultimate.pin20
  N5: Arduino_Nano.D6, SwinSid_Ultimate.pin21
  N6: Arduino_Nano.D7, SwinSid_Ultimate.pin22
  N7: Arduino_Nano.D8, SwinSid_Ultimate.pin15
  N8: Arduino_Nano.D9, SwinSid_Ultimate.pin16
  N9: Arduino_Nano.D10, SwinSid_Ultimate.pin6
  N10: Arduino_Nano.D11/MOSI, SwinSid_Ultimate.pin7
  N11: Arduino_Nano.D12/MISO, SwinSid_Ultimate.pin5
  N12: Arduino_Nano.5V, SwinSid_Ultimate.pin25
  N13: Arduino_Nano.A4, SwinSid_Ultimate.pin13
  N14: Arduino_Nano.A3, SwinSid_Ultimate.pin12
  N15: Arduino_Nano.A2, SwinSid_Ultimate.pin11
  N16: Arduino_Nano.A1, SwinSid_Ultimate.pin10
  N17: Arduino_Nano.A0, SwinSid_Ultimate.pin9
  N18: Arduino_Nano.D13/SCK, SwinSid_Ultimate.pin8
  N19: Audio_Out.RIGHT, Audio_Out.LEFT, C1.-
  N20: C1.+, SwinSid_Ultimate.pin27
  N21: SwinSid_Ultimate.pin1, C2.+
  N22: SwinSid_Ultimate.pin2, C2.-
  N23: SwinSid_Ultimate.pin3, C3.+
  N24: SwinSid_Ultimate.pin4, C3.-

notes:
  USB
